// Logisim project Assignment Simulation.circ as structural Verilog: 1 circuit, main circuit main
module main (
  input  exit,
  input  entry,
  input  exit_2,
  input  entry_2,
  output [3:0] out_5,
  output [3:0] out_6,
  output out_7,
  output [3:0] out_8,
  output [3:0] out_9,
  output out_10
);

  wire and_1_out, and_2_out, and_3_out, and_4_out, and_5_out, clock_1_out, clock_2_out, comparator_1_gt,
       comparator_2_eq, comparator_2_gt, counter_3_carry, counter_4_carry, n7_segment_display_driver_1_a_2,
       n7_segment_display_driver_1_b_2, n7_segment_display_driver_1_c_2, n7_segment_display_driver_1_d_2,
       n7_segment_display_driver_1_e, n7_segment_display_driver_1_f, n7_segment_display_driver_1_g,
       n7_segment_display_driver_2_a_2, n7_segment_display_driver_2_b_2, n7_segment_display_driver_2_c_2,
       n7_segment_display_driver_2_d_2, n7_segment_display_driver_2_e, n7_segment_display_driver_2_f,
       n7_segment_display_driver_2_g, n7_segment_display_driver_3_a_2, n7_segment_display_driver_3_b_2,
       n7_segment_display_driver_3_c_2, n7_segment_display_driver_3_d_2, n7_segment_display_driver_3_e,
       n7_segment_display_driver_3_f, n7_segment_display_driver_3_g, n7_segment_display_driver_4_a_2,
       n7_segment_display_driver_4_b_2, n7_segment_display_driver_4_c_2, n7_segment_display_driver_4_d_2,
       n7_segment_display_driver_4_e, n7_segment_display_driver_4_f, n7_segment_display_driver_4_g,
       n7_segment_display_driver_5_a_2, n7_segment_display_driver_5_b_2, n7_segment_display_driver_5_c_2,
       n7_segment_display_driver_5_d_2, n7_segment_display_driver_5_e, n7_segment_display_driver_5_f,
       n7_segment_display_driver_5_g, nor_1_out, nor_3_out, not_1_out, or_1_out, xor_1_out, xor_2_out;

  _7_segment_display_driver u_7_segment_display_driver_1 (
    .D(out_5[3]), .C(out_5[2]), .B(out_5[1]), .A(out_5[0]), .a_2(n7_segment_display_driver_1_a_2),
    .b_2(n7_segment_display_driver_1_b_2), .c_2(n7_segment_display_driver_1_c_2),
    .d_2(n7_segment_display_driver_1_d_2), .e(n7_segment_display_driver_1_e),
    .f(n7_segment_display_driver_1_f), .g(n7_segment_display_driver_1_g));
  and and_1 (and_1_out, out_7, counter_3_carry);
  _7_segment_display_driver u_7_segment_display_driver_2 (
    .D(out_8[3]), .C(out_8[2]), .B(out_8[1]), .A(out_8[0]), .a_2(n7_segment_display_driver_2_a_2),
    .b_2(n7_segment_display_driver_2_b_2), .c_2(n7_segment_display_driver_2_c_2),
    .d_2(n7_segment_display_driver_2_d_2), .e(n7_segment_display_driver_2_e),
    .f(n7_segment_display_driver_2_f), .g(n7_segment_display_driver_2_g));
  and and_2 (and_2_out, out_10, counter_4_carry);
  _7_Segment_Display u_7_segment_display_1 (
    .g(n7_segment_display_driver_1_g), .f(n7_segment_display_driver_1_f),
    .a(n7_segment_display_driver_1_a_2), .b(n7_segment_display_driver_1_b_2),
    .e(n7_segment_display_driver_1_e), .d(n7_segment_display_driver_1_d_2),
    .c(n7_segment_display_driver_1_c_2));  // open: dp
  Counter #(.width(4), .max('h9)) counter_1 (
    .load(and_1_out), .count(counter_3_carry), .Q(out_5), .clk(and_3_out));  // open: D, carry, clr
  _7_Segment_Display u_7_segment_display_2 (
    .g(n7_segment_display_driver_2_g), .f(n7_segment_display_driver_2_f),
    .a(n7_segment_display_driver_2_a_2), .b(n7_segment_display_driver_2_b_2),
    .e(n7_segment_display_driver_2_e), .d(n7_segment_display_driver_2_d_2),
    .c(n7_segment_display_driver_2_c_2));  // open: dp
  Counter #(.width(4), .max('h9)) counter_2 (
    .load(and_2_out), .count(counter_4_carry), .Q(out_8), .clk(and_4_out));  // open: D, carry, clr
  Counter #(.width(4), .max('h9)) counter_3 (
    .load(out_7), .count(1'b1), .Q(out_6), .carry(counter_3_carry), .clk(and_3_out));  // open: D, clr
  Counter #(.width(4), .max('h9)) counter_4 (
    .load(out_10), .count(1'b1), .Q(out_9), .carry(counter_4_carry), .clk(and_4_out));  // open: D, clr
  and and_3 (and_3_out, clock_1_out, xor_1_out);
  Clock clock_1 (.out(clock_1_out));
  and and_4 (and_4_out, clock_2_out, xor_2_out);
  Clock clock_2 (.out(clock_2_out));
  _7_segment_display_driver u_7_segment_display_driver_3 (
    .D(out_6[3]), .C(out_6[2]), .B(out_6[1]), .A(out_6[0]), .a_2(n7_segment_display_driver_3_a_2),
    .b_2(n7_segment_display_driver_3_b_2), .c_2(n7_segment_display_driver_3_c_2),
    .d_2(n7_segment_display_driver_3_d_2), .e(n7_segment_display_driver_3_e),
    .f(n7_segment_display_driver_3_f), .g(n7_segment_display_driver_3_g));
  nor nor_1 (nor_1_out, entry, out_7);
  nor nor_2 (out_7, nor_1_out, exit);
  xor xor_1 (xor_1_out, exit, entry);
  _7_segment_display_driver u_7_segment_display_driver_4 (
    .D(out_9[3]), .C(out_9[2]), .B(out_9[1]), .A(out_9[0]), .a_2(n7_segment_display_driver_4_a_2),
    .b_2(n7_segment_display_driver_4_b_2), .c_2(n7_segment_display_driver_4_c_2),
    .d_2(n7_segment_display_driver_4_d_2), .e(n7_segment_display_driver_4_e),
    .f(n7_segment_display_driver_4_f), .g(n7_segment_display_driver_4_g));
  nor nor_3 (nor_3_out, entry_2, out_10);
  nor nor_4 (out_10, nor_3_out, exit_2);
  xor xor_2 (xor_2_out, exit_2, entry_2);
  _7_Segment_Display u_7_segment_display_3 (
    .g(n7_segment_display_driver_3_g), .f(n7_segment_display_driver_3_f),
    .a(n7_segment_display_driver_3_a_2), .b(n7_segment_display_driver_3_b_2),
    .e(n7_segment_display_driver_3_e), .d(n7_segment_display_driver_3_d_2),
    .c(n7_segment_display_driver_3_c_2));  // open: dp
  _7_Segment_Display u_7_segment_display_4 (
    .g(n7_segment_display_driver_4_g), .f(n7_segment_display_driver_4_f),
    .a(n7_segment_display_driver_4_a_2), .b(n7_segment_display_driver_4_b_2),
    .e(n7_segment_display_driver_4_e), .d(n7_segment_display_driver_4_d_2),
    .c(n7_segment_display_driver_4_c_2));  // open: dp
  LED u_entry (.in(exit_2));
  LED u_entry_2 (.in(exit));
  LED u_exit (.in(entry_2));
  LED u_exit_2 (.in(entry));
  Comparator #(.width(4), .mode("unsigned")) comparator_1 (.a(out_6), .b(out_9), .gt(comparator_1_gt));  // open: eq, lt
  Comparator #(.width(4), .mode("unsigned")) comparator_2 (
    .a(out_5), .b(out_8), .gt(comparator_2_gt), .eq(comparator_2_eq));  // open: lt
  not not_1 (not_1_out, or_1_out);
  and and_5 (and_5_out, comparator_2_eq, comparator_1_gt);
  _7_segment_display_driver u_7_segment_display_driver_5 (
    .D(1'b0), .C(1'b0), .B(or_1_out), .A(not_1_out), .a_2(n7_segment_display_driver_5_a_2),
    .b_2(n7_segment_display_driver_5_b_2), .c_2(n7_segment_display_driver_5_c_2),
    .d_2(n7_segment_display_driver_5_d_2), .e(n7_segment_display_driver_5_e),
    .f(n7_segment_display_driver_5_f), .g(n7_segment_display_driver_5_g));
  or or_1 (or_1_out, comparator_2_gt, and_5_out);
  _7_Segment_Display u_7_segment_display_5 (
    .g(n7_segment_display_driver_5_g), .f(n7_segment_display_driver_5_f),
    .a(n7_segment_display_driver_5_a_2), .b(n7_segment_display_driver_5_b_2),
    .e(n7_segment_display_driver_5_e), .d(n7_segment_display_driver_5_d_2),
    .c(n7_segment_display_driver_5_c_2));  // open: dp

  // Notes on the sheet:
  //   second
  //   second
  //   first
  //   first
  //   counter clk 
  //   counter clk 
  //   SECOND FLOOR
  //   FIRST FLOOR
  //   tens place
  //   units place
  //   FLOOR NUMBER WITH MORE EMPTY SLOTS
  //   second floor
endmodule
